// Logisim project alu.circ as structural Verilog: 3 circuits, main circuit 1-bit
module _1_bit (
  input  [1:0] s,
  input  Ci,
  input  Ai,
  input  Bi,
  output Fi,
  output Ci_2
);

  wire and_1_out, and_2_out, and_3_out, and_4_out, not_1_out, not_2_out, not_3_out, Xi_out, Yi_out, Zi_out;

  not not_1 (not_1_out, s[1]);
  not not_2 (not_2_out, s[0]);
  not not_3 (not_3_out, Bi);
  and and_1 (and_1_out, s[1], not_2_out, Bi);
  and and_2 (and_2_out, not_1_out, not_2_out);
  and and_3 (and_3_out, s[0], not_3_out);
  and and_4 (and_4_out, s[1], s[0]);
  or Xi (Xi_out, Ai, and_1_out);
  or Yi (Yi_out, and_2_out, and_3_out, and_4_out);
  and Zi (Zi_out, not_1_out, Ci);
  Adder #(.width(1)) adder_1 (.a(Xi_out), .b(Yi_out), .out(Fi), .cin(Zi_out), .cout(Ci_2));
endmodule

module _4_bit (
  input  [3:0] A,
  input  [3:0] B,
  input  cs2,
  input  [1:0] cs1__cs0,
  output out_5,
  output out_6,
  output out_7,
  output out_8,
  output [3:0] F,
  output Cout
);

  wire n1_bit_1_ci_2, n1_bit_2_ci_2, n1_bit_3_ci_2;

  _1_bit u_1_bit_1 (.Fi(F[0]), .Ci_2(n1_bit_1_ci_2), .s(cs1__cs0), .Ai(A[0]), .Bi(B[0]), .Ci(cs2));
  _1_bit u_1_bit_2 (.Fi(F[1]), .Ci_2(n1_bit_2_ci_2), .s(cs1__cs0), .Ai(A[1]), .Bi(B[1]), .Ci(n1_bit_1_ci_2));
  _1_bit u_1_bit_3 (.Fi(F[2]), .Ci_2(n1_bit_3_ci_2), .s(cs1__cs0), .Ai(A[2]), .Bi(B[2]), .Ci(n1_bit_2_ci_2));
  _1_bit u_1_bit_4 (.Fi(F[3]), .Ci_2(Cout), .s(cs1__cs0), .Ai(A[3]), .Bi(B[3]), .Ci(n1_bit_3_ci_2));
  status status_1 (.C(out_5), .V(out_6), .Z(out_7), .S(out_8), .in_1(F), .C4(n1_bit_3_ci_2), .C5(Cout));
endmodule

module status (
  input  [3:0] in_1,
  input  C4,
  input  C5,
  output C,
  output V,
  output Z,
  output S
);

  nor nor_1 (Z, in_1[0], in_1[1], in_1[2], in_1[3]);
  xor xor_1 (V, C5, C4);

  assign C = C5;
  assign S = in_1[3];
endmodule
