// Logisim project Comparator.circ as structural Verilog: 1 circuit, main circuit comparator
module comparator (
  input  [12:0] Significand_A,
  input  [3:0] Exponent_A,
  input  [12:0] Significand_B,
  input  [3:0] Exponent_B,
  output [11:0] Larger_Significand,
  output Larger_Sign,
  output [11:0] Smaller_Significand,
  output Smaller_Sign,
  output [3:0] Exponent_Out
);

  wire subtractor_1_bout;
  wire [3:0] multiplexer_4_out, negator_1_out, subtractor_1_out;
  wire [11:0] multiplexer_1_out;

  Subtractor #(.width(4)) subtractor_1 (
    .a(Exponent_A), .b(Exponent_B), .out(subtractor_1_out), .bout(subtractor_1_bout));  // open: bin
  Multiplexer #(.width(13), .enable("false")) multiplexer_1 (
    .in0(Significand_B), .in1(Significand_A), .out({Smaller_Sign, multiplexer_1_out}), .sel(subtractor_1_bout));
  Multiplexer #(.width(4), .enable("false")) multiplexer_2 (
    .in0(Exponent_A), .in1(Exponent_B), .out(Exponent_Out), .sel(subtractor_1_bout));
  Multiplexer #(.width(13), .enable("false")) multiplexer_3 (
    .in0(Significand_A), .in1(Significand_B), .out({Larger_Sign, Larger_Significand}), .sel(subtractor_1_bout));
  Negator #(.width(4)) negator_1 (.in(subtractor_1_out), .out(negator_1_out));
  Multiplexer #(.width(4), .enable("false")) multiplexer_4 (
    .in0(subtractor_1_out), .in1(negator_1_out), .out(multiplexer_4_out), .sel(subtractor_1_bout));
  Shifter #(.width(12), .shift("lr")) shifter_1 (
    .in(multiplexer_1_out), .\dist (multiplexer_4_out), .out(Smaller_Significand));
endmodule
