// Logisim project Separator.circ as structural Verilog: 1 circuit, main circuit separator
module separator (
  input  [15:0] FP_Number,
  output [11:0] Significand,
  output [3:0] Exponent,
  output Sign
);


  assign Exponent = FP_Number[14:11];
  assign Sign = FP_Number[15];
  assign Significand = {1'b1, FP_Number[10:0]};
endmodule
