// Logisim project SignficandAddition.circ as structural Verilog: 1 circuit, main circuit Significand Addition
module Significand_Addition (
  input  sign_1,
  input  [11:0] in_2,
  input  [11:0] in_3,
  input  sign_2,
  output [15:0] out_5,
  output sign
);

  wire [14:0] adder_1_out;
  wire [15:0] bit_extender_1_out, bit_extender_2_out, multiplexer_1_out, multiplexer_2_out, negator_1_out,
       negator_2_out, negator_3_out;

  assign bit_extender_1_out = {{4{1'b0}}, in_2};  // Bit_Extender bit_extender_1
  assign bit_extender_2_out = {{4{1'b0}}, in_3};  // Bit_Extender bit_extender_2
  Negator #(.width(16)) negator_1 (.in(bit_extender_1_out), .out(negator_1_out));
  Negator #(.width(16)) negator_2 (.in(bit_extender_2_out), .out(negator_2_out));
  Multiplexer #(.width(16), .enable("false")) multiplexer_1 (
    .in0(bit_extender_1_out), .in1(negator_1_out), .out(multiplexer_1_out), .sel(sign_1));
  Multiplexer #(.width(16), .enable("false")) multiplexer_2 (
    .in0(bit_extender_2_out), .in1(negator_2_out), .out(multiplexer_2_out), .sel(sign_2));
  Adder #(.width(16)) adder_1 (
    .a(multiplexer_1_out), .b(multiplexer_2_out), .out({sign, adder_1_out}), .cin(1'b0));  // open: cout
  Negator #(.width(16)) negator_3 (.in({sign, adder_1_out}), .out(negator_3_out));
  Multiplexer #(.width(16), .enable("false")) multiplexer_3 (
    .in0({sign, adder_1_out}), .in1(negator_3_out), .out(out_5), .sel(sign));

  // Notes on the sheet:
  //   Large Significand
  //   Small Significand
  //   added significand
endmodule
