// Logisim project fpadder.circ as structural Verilog: 2 circuits, main circuit fpadder
module fpadder (
  input  [15:0] Input_1,
  input  [15:0] Input_2,
  output [15:0] Output,
  output Overflow,
  output Underflow
);

  wire comparator_1_larger_sign, comparator_1_smaller_sign;
  wire [3:0] comparator_1_exponent_out, separator_1_exponent, separator_2_exponent;
  wire [11:0] comparator_1_larger_significand, comparator_1_smaller_significand, separator_1_significand,
       separator_2_significand;
  wire [12:12] separator_1_sign, separator_2_sign;
  wire [15:0] significand_addition_1_out_5;

  separator separator_1 (
    .FP_Number(Input_1), .Significand(separator_1_significand), .Exponent(separator_1_exponent),
    .Sign(separator_1_sign[12]));
  separator separator_2 (
    .FP_Number(Input_2), .Significand(separator_2_significand), .Exponent(separator_2_exponent),
    .Sign(separator_2_sign[12]));
  comparator comparator_1 (
    .Significand_A({separator_1_sign[12], separator_1_significand}), .Exponent_A(separator_1_exponent),
    .Significand_B({separator_2_sign[12], separator_2_significand}), .Exponent_B(separator_2_exponent),
    .Larger_Significand(comparator_1_larger_significand),
    .Smaller_Significand(comparator_1_smaller_significand), .Exponent_Out(comparator_1_exponent_out),
    .Larger_Sign(comparator_1_larger_sign), .Smaller_Sign(comparator_1_smaller_sign));
  normalizer normalizer_1 (
    .Exponent_In(comparator_1_exponent_out), .Significand_In(significand_addition_1_out_5),
    .Underflow(Underflow), .Overflow(Overflow), .Significand_Out(Output[10:0]), .Exponent_Out(Output[14:11]));
  Significand_Addition significand_addition_1 (
    .sign_1(comparator_1_larger_sign), .in_2(comparator_1_larger_significand),
    .in_3(comparator_1_smaller_significand), .sign_2(comparator_1_smaller_sign),
    .out_5(significand_addition_1_out_5), .sign(Output[15]));

  // Notes on the sheet:
  //   Separator
  //   Separator
  //   Comparator
  //   Adder
  //   Normalizer
endmodule

module main (
  input  [15:0] Input_1,
  input  [15:0] Input_2,
  output [15:0] Output,
  output Overflow,
  output Underflow
);

  fpadder fpadder_1 (.Input_2(Input_2), .Input_1(Input_1), .Output(Output), .Overflow(Overflow), .Underflow(Underflow));
endmodule
