// Logisim project normalizer.circ as structural Verilog: 3 circuits, main circuit normalizer
module bitfinder (
  input  [12:0] Input,
  output [3:0] Position,
  output present
);

  wire [3:0] bitfinder_1_index;

  BitFinder #(.width(13), .\type ("high1")) bitfinder_1 (.in(Input), .index(bitfinder_1_index), .found(present));
  Subtractor #(.width(4)) subtractor_1 (.a(4'b1011), .b(bitfinder_1_index), .out(Position));  // open: bin, bout
endmodule

module normalizer (
  input  [15:0] Significand_In,
  input  [3:0] Exponent_In,
  output [3:0] Exponent_Out,
  output [10:0] Significand_Out,
  output Underflow,
  output Overflow
);

  wire and_1_out, nand_1_out, nor_1_out, not_1_out, subtractor_1_bout;
  wire [3:0] bitfinder_1_position;
  wire [12:11] shifter_1_shift_out;

  nand nand_1 (nand_1_out, bitfinder_1_position[3], bitfinder_1_position[2], bitfinder_1_position[1], bitfinder_1_position[0]);
  and and_1 (and_1_out, nand_1_out, subtractor_1_bout);
  Subtractor #(.width(4)) subtractor_1 (
    .a(Exponent_In), .b(bitfinder_1_position), .out(Exponent_Out), .bout(subtractor_1_bout));  // open: bin
  nor nor_1 (nor_1_out, Exponent_Out[3], Exponent_Out[2], Exponent_Out[1], Exponent_Out[0]);
  or or_1 (Underflow, and_1_out, nor_1_out);
  bitfinder bitfinder_1 (.Input(Significand_In[12:0]), .Position(bitfinder_1_position));  // open: present
  not not_1 (not_1_out, and_1_out);
  and and_2 (Overflow, Exponent_Out[3], Exponent_Out[2], not_1_out, Exponent_Out[1], Exponent_Out[0]);
  shifter shifter_1 (
    .Shift_In(Significand_In[12:0]), .Shift(bitfinder_1_position),
    .Shift_Out({shifter_1_shift_out, Significand_Out}));
endmodule

module shifter (
  input  [12:0] Shift_In,
  input  [3:0] Shift,
  output [12:0] Shift_Out
);

  wire and_1_out;
  wire [3:0] multiplexer_1_out;

  and and_1 (and_1_out, Shift[0], Shift[1], Shift[2], Shift[3]);
  Multiplexer #(.width(4), .enable("false")) multiplexer_1 (
    .in0(Shift), .in1(4'b1100), .out(multiplexer_1_out), .sel(and_1_out));
  Shifter #(.width(13), .shift("rl")) shifter_1 (.in(Shift_In), .\dist (multiplexer_1_out), .out(Shift_Out));
endmodule
