// Logisim project MIPS.circ as structural Verilog: 5 circuits, main circuit main
module main (
  input  CLEAR,
  input  in_2
);

  wire alu_1_zf, and_1_out, and_2_out, clock_1_out, control_1_out_3, control_1_out_4, control_1_out_5,
       control_1_out_6, control_1_out_7, control_1_out_8, control_1_out_9, control_1_out_10,
       control_1_out_11, not_1_out, or_1_out;
  wire [2:0] control_1_alu_op;
  wire [3:0] instructions_1__0_3, instructions_1__4_7, instructions_1__16_19, multiplexer_1_out;
  wire [7:0] adder_1_out, adder_2_out, alu_1_f, instructions_1__8_11, multiplexer_2_out, multiplexer_3_out,
       multiplexer_4_out, multiplexer_5_out, PC_q, ram_1_data, register_file_1_read_data_1,
       register_file_1_read_data_2;

  Clock clock_1 (.out(clock_1_out));
  Register #(.trigger("falling")) PC (.D(multiplexer_4_out), .Q(PC_q), .clk(clock_1_out), .clr(CLEAR));  // open: en
  Adder adder_1 (.a(PC_q), .b(8'h1), .out(adder_1_out));  // open: cin, cout
  Instructions instructions_1 (
    .PC(PC_q), ._16_19(instructions_1__16_19), ._12_15(instructions_1__8_11[7:4]),
    ._8_11(instructions_1__8_11[3:0]), ._4_7(instructions_1__4_7), ._0_3(instructions_1__0_3));
  Multiplexer #(.width(4), .enable("false")) multiplexer_1 (
    .in0(instructions_1__8_11[3:0]), .in1(instructions_1__4_7), .out(multiplexer_1_out),
    .sel(control_1_out_11));
  Control control_1 (
    .OP_Code(instructions_1__16_19), .ALU_OP(control_1_alu_op), .out_3(control_1_out_3),
    .out_4(control_1_out_4), .out_5(control_1_out_5), .out_6(control_1_out_6), .out_7(control_1_out_7),
    .out_8(control_1_out_8), .out_9(control_1_out_9), .out_10(control_1_out_10), .out_11(control_1_out_11));
  Register_File register_file_1 (
    .Dst_Reg_1(multiplexer_1_out), .Write_Data(multiplexer_5_out), .Src_Reg_1(instructions_1__8_11[7:4]),
    .Src_Reg_2(instructions_1__8_11[3:0]), .RegWrite(control_1_out_8),
    .Read_Data_1(register_file_1_read_data_1), .Read_Data_2(register_file_1_read_data_2),
    .clk_prime(clock_1_out));
  Adder adder_2 (
    .a(adder_1_out), .b({instructions_1__4_7, instructions_1__0_3}), .out(adder_2_out));  // open: cin, cout
  Multiplexer #(.width(8), .enable("false")) multiplexer_2 (
    .in0(register_file_1_read_data_2), .in1({instructions_1__4_7, instructions_1__0_3}),
    .out(multiplexer_2_out), .sel(control_1_out_10));
  Multiplexer #(.width(8), .enable("false")) multiplexer_3 (
    .in0(adder_1_out), .in1(adder_2_out), .out(multiplexer_3_out), .sel(or_1_out));
  or or_1 (or_1_out, and_1_out, and_2_out);
  and and_1 (and_1_out, control_1_out_5, alu_1_zf);
  and and_2 (and_2_out, not_1_out, control_1_out_4);
  not not_1 (not_1_out, alu_1_zf);
  ALU alu_1 (
    .A(register_file_1_read_data_1), .B(multiplexer_2_out), .ALUop(control_1_alu_op), .ZF(alu_1_zf),
    .F(alu_1_f));
  Multiplexer #(.width(8), .enable("false")) multiplexer_4 (
    .in0(multiplexer_3_out), .in1(instructions_1__8_11), .out(multiplexer_4_out), .sel(control_1_out_3));
  RAM #(.bus("separate")) ram_1 (
    .addr(alu_1_f), .din(register_file_1_read_data_2), .data(ram_1_data), .str(control_1_out_6),
    .clk(clock_1_out), .ld(control_1_out_7));  // open: sel, clr
  Multiplexer #(.width(8), .enable("false")) multiplexer_5 (
    .in0(alu_1_f), .in1(ram_1_data), .out(multiplexer_5_out), .sel(control_1_out_9));

  // Notes on the sheet:
  //   Instruction Memory
  //   Data Memory
endmodule

module Register_File (
  input  RegWrite,
  input  clk_prime,
  input  [3:0] Dst_Reg_1,
  input  [7:0] Write_Data,
  input  [3:0] Src_Reg_1,
  input  [3:0] Src_Reg_2,
  output [7:0] Read_Data_1,
  output [7:0] Read_Data_2
);

  wire and_1_out, demultiplexer_1_out1, demultiplexer_1_out2, demultiplexer_1_out3, demultiplexer_1_out4,
       demultiplexer_1_out5, demultiplexer_1_out6, demultiplexer_1_out7;
  wire [7:0] _0___zero_q, _1___t0_q, _2___t1_q, _3___t2_q, _4___t3_q, _5___t4_q, _6___sp_q, _7___t5_q;

  Register _0___zero (.Q(_0___zero_q));  // open: D, en, clk, clr
  Register _1___t0 (.D(Write_Data), .Q(_1___t0_q), .clk(demultiplexer_1_out1));  // open: en, clr
  Register _2___t1 (.D(Write_Data), .Q(_2___t1_q), .clk(demultiplexer_1_out2));  // open: en, clr
  Multiplexer #(.select(3), .width(8), .enable("false")) multiplexer_1 (
    .in0(_0___zero_q), .in1(_1___t0_q), .in2(_2___t1_q), .in3(_3___t2_q), .in4(_4___t3_q), .in5(_5___t4_q),
    .in6(_6___sp_q), .in7(_7___t5_q), .out(Read_Data_1), .sel(Src_Reg_1[2:0]));
  Demultiplexer #(.select(3), .enable("false")) demultiplexer_1 (
    .out1(demultiplexer_1_out1), .out2(demultiplexer_1_out2), .out3(demultiplexer_1_out3),
    .out4(demultiplexer_1_out4), .out5(demultiplexer_1_out5), .out6(demultiplexer_1_out6),
    .out7(demultiplexer_1_out7), .in(and_1_out), .sel(Dst_Reg_1[2:0]));  // open: out0
  Register _3___t2 (.D(Write_Data), .Q(_3___t2_q), .clk(demultiplexer_1_out3));  // open: en, clr
  and and_1 (and_1_out, RegWrite, clk_prime);
  Register _4___t3 (.D(Write_Data), .Q(_4___t3_q), .clk(demultiplexer_1_out4));  // open: en, clr
  Multiplexer #(.select(3), .width(8), .enable("false")) multiplexer_2 (
    .in0(_0___zero_q), .in1(_1___t0_q), .in2(_2___t1_q), .in3(_3___t2_q), .in4(_4___t3_q), .in5(_5___t4_q),
    .in6(_6___sp_q), .in7(_7___t5_q), .out(Read_Data_2), .sel(Src_Reg_2[2:0]));
  Register _5___t4 (.D(Write_Data), .Q(_5___t4_q), .clk(demultiplexer_1_out5));  // open: en, clr
  Register _6___sp (.D(Write_Data), .Q(_6___sp_q), .clk(demultiplexer_1_out6));  // open: en, clr
  Register _7___t5 (.D(Write_Data), .Q(_7___t5_q), .clk(demultiplexer_1_out7));  // open: en, clr
endmodule

module Instructions (
  input  [7:0] PC,
  output [3:0] _16_19,
  output [3:0] _12_15,
  output [3:0] _8_11,
  output [3:0] _4_7,
  output [3:0] _0_3
);

  ROM #(.dataWidth(20)) rom_1 (.addr(PC), .data({_16_19, _12_15, _8_11, _4_7, _0_3}));  // open: sel

  // Notes on the sheet:
  //   contents of rom_1 (hex, n*v repeats v):
  //   f06ff f0105 61205 11240 54101 21b00 e1502 b5420 2150 95420 82200 a2114 42103 72203 c2201 21a00 46200
  //   66601 46100 66601 f6601 76200 f6601 76100 21b00 312f6
endmodule

module Control (
  input  [3:0] OP_Code,
  output [2:0] ALU_OP,
  output out_3,
  output out_4,
  output out_5,
  output out_6,
  output out_7,
  output out_8,
  output out_9,
  output out_10,
  output out_11
);

  ROM #(.addrWidth(4), .dataWidth(12)) rom_1 (
    .addr(OP_Code), .data({out_11, out_10, out_9, out_8, out_7, out_6, out_5, out_4, out_3, ALU_OP}));  // open: sel

  // Notes on the sheet:
  //   contents of rom_1 (hex, n*v repeats v):
  //   902 900 8 11 440 21 501 780 503 904 502 901 506 903 505 500
endmodule

module ALU (
  input  [7:0] A,
  input  [7:0] B,
  input  [2:0] ALUop,
  output ZF,
  output [7:0] F
);

  wire [7:0] adder_1_out, and_1_out, nor_1_out, or_1_out, subtractor_1_out;
  wire [15:0] shifter_1_out, shifter_2_out;

  Adder adder_1 (.a(A), .b(B), .out(adder_1_out), .cin(1'b0));  // open: cout
  Subtractor subtractor_1 (.a(A), .b(B), .out(subtractor_1_out), .bin(1'b0));  // open: bout
  assign or_1_out = A | B;  // OR_Gate or_1, 8 bits wide
  assign and_1_out = A & B;  // AND_Gate and_1, 8 bits wide
  assign nor_1_out = ~(A | B);  // NOR_Gate nor_1, 8 bits wide
  Shifter #(.width(16)) shifter_1 (.in({{8{1'b0}}, A}), .\dist (B[3:0]), .out(shifter_1_out));
  Shifter #(.width(16), .shift("lr")) shifter_2 (.in({{8{1'b0}}, A}), .\dist (B[3:0]), .out(shifter_2_out));
  Multiplexer #(.select(3), .width(8), .enable("false")) multiplexer_1 (
    .in0(adder_1_out), .in1(subtractor_1_out), .in2(or_1_out), .in3(and_1_out), .in4(nor_1_out),
    .in5(shifter_1_out[7:0]), .in6(shifter_2_out[7:0]), .in7({8{1'b0}}), .out(F), .sel(ALUop));
  nor nor_2 (ZF, F[0], F[1], F[2], F[3], F[4], F[5], F[6], F[7]);
endmodule
