// Logisim project Memory.circ as structural Verilog
module Register_File (
  input  RegWrite,
  input  [3:0] Dst_Reg_1,
  input  [7:0] Write_Data,
  input  [3:0] Src_Reg_1,
  input  [3:0] Src_Reg_2,
  output [7:0] Read_Data_1,
  output [7:0] Output_2
);

  wire demultiplexer_1_out0, demultiplexer_1_out1, demultiplexer_1_out2, demultiplexer_1_out3,
       demultiplexer_1_out4, demultiplexer_1_out5;
  wire [7:0] _0___zero_q, _1___t0_q, _2___t1_q, _3___t2_q, _4___t3_q, _5___t4_q;

  Register _0___zero (.D(Write_Data), .Q(_0___zero_q), .clk(demultiplexer_1_out0));  // open: en, clr
  Register _1___t0 (.D(Write_Data), .Q(_1___t0_q), .clk(demultiplexer_1_out1));  // open: en, clr
  Multiplexer #(.select(3), .width(8), .enable("false")) multiplexer_1 (
    .in0(_0___zero_q), .in1(_1___t0_q), .in2(_2___t1_q), .in3(_3___t2_q), .in4(_4___t3_q), .in5(_5___t4_q),
    .out(Read_Data_1), .sel(Src_Reg_1[2:0]));  // open: in6, in7
  Register _2___t1 (.D(Write_Data), .Q(_2___t1_q), .clk(demultiplexer_1_out2));  // open: en, clr
  Demultiplexer #(.select(3), .enable("false")) demultiplexer_1 (
    .out0(demultiplexer_1_out0), .out1(demultiplexer_1_out1), .out2(demultiplexer_1_out2),
    .out3(demultiplexer_1_out3), .out4(demultiplexer_1_out4), .out5(demultiplexer_1_out5), .in(RegWrite),
    .sel(Dst_Reg_1[2:0]));  // open: out6, out7
  Register _3___t2 (.D(Write_Data), .Q(_3___t2_q), .clk(demultiplexer_1_out3));  // open: en, clr
  Register _4___t3 (.D(Write_Data), .Q(_4___t3_q), .clk(demultiplexer_1_out4));  // open: en, clr
  Multiplexer #(.select(3), .width(8), .enable("false")) multiplexer_2 (
    .in0(_0___zero_q), .in1(_1___t0_q), .in2(_2___t1_q), .in3(_3___t2_q), .in4(_4___t3_q), .in5(_5___t4_q),
    .out(Output_2), .sel(Src_Reg_2[2:0]));  // open: in6, in7
  Register _5___t4 (.D(Write_Data), .Q(_5___t4_q), .clk(demultiplexer_1_out5));  // open: en, clr
endmodule

module Instructions (
  input  [7:0] PC,
  input  in_2,
  output [3:0] _16_19,
  output [3:0] _12_15,
  output [3:0] _8_11,
  output [3:0] _4_7,
  output [3:0] _0_3
);

  RAM #(.dataWidth(20)) ram_1 (
    .addr(PC), .data({_16_19, _12_15, _8_11, _4_7, _0_3}), .clk(in_2), .ld(1'b1));  // open: sel, clr
endmodule
