// Logisim project Control.circ as structural Verilog: 1 circuit, main circuit Control Signal
module Control_Signal (
  input  [3:0] OP_Code,
  output [2:0] ALU_OP,
  output out_3,
  output out_4,
  output out_5,
  output out_6,
  output out_7,
  output out_8,
  output out_9,
  output out_10,
  output out_11
);

  ROM #(.addrWidth(4), .dataWidth(12)) rom_1 (
    .addr(OP_Code), .data({out_11, out_10, out_9, out_8, out_7, out_6, out_5, out_4, out_3, ALU_OP}));  // open: sel

  // Notes on the sheet:
  //   contents of rom_1 (hex, n*v repeats v):
  //   902 900 8 11 440 21 501 780 503 904 502 901 906 903 905 500
endmodule
