// Logisim project Forward Unit.circ as structural Verilog: 4 circuits, main circuit Hazard Checker
module Hazard_Checker (
  input  EX_MEM_RW,
  input  [3:0] EX_MEM_RD,
  input  [3:0] ID_EX_RS,
  output EX_Hazard
);

  wire and_1_out, nor_1_out, or_1_out, subtractor_1_bout;
  wire [3:0] subtractor_1_out;

  or or_1 (or_1_out, EX_MEM_RD[0], EX_MEM_RD[1], EX_MEM_RD[2], EX_MEM_RD[3]);
  Subtractor #(.width(4)) subtractor_1 (
    .a(EX_MEM_RD), .b(ID_EX_RS), .out(subtractor_1_out), .bout(subtractor_1_bout));  // open: bin
  and and_1 (and_1_out, EX_MEM_RW, or_1_out);
  nor nor_1 (nor_1_out, subtractor_1_out[0], subtractor_1_out[1], subtractor_1_out[2], subtractor_1_out[3], subtractor_1_bout);
  and and_2 (EX_Hazard, and_1_out, nor_1_out);
endmodule

module Memory_Hazard_Checker (
  input  MEM_WB_RegWrite,
  input  [3:0] MEM_WB_RD,
  input  [3:0] ID_EX_Rs,
  input  EX_Hazard,
  output MEM_Hazard
);

  wire hazard_checker_1_ex_hazard, not_1_out;

  not not_1 (not_1_out, EX_Hazard);
  Hazard_Checker hazard_checker_1 (
    .EX_MEM_RW(MEM_WB_RegWrite), .EX_MEM_RD(MEM_WB_RD), .ID_EX_RS(ID_EX_Rs),
    .EX_Hazard(hazard_checker_1_ex_hazard));
  and and_1 (MEM_Hazard, hazard_checker_1_ex_hazard, not_1_out);
endmodule

module Forward_Bit_Generator (
  input  EX_MEM_RegWrite,
  input  [3:0] EX_MEM_RegisterRd,
  input  [3:0] ID_EX_RegisterRs,
  input  MEM_WB_RegWrite,
  input  [3:0] MEM_WB_RegisterRd,
  output [1:0] Forward
);

  wire hazard_checker_1_ex_hazard, not_1_out;

  Hazard_Checker hazard_checker_1 (
    .EX_MEM_RW(EX_MEM_RegWrite), .EX_MEM_RD(EX_MEM_RegisterRd), .ID_EX_RS(ID_EX_RegisterRs),
    .EX_Hazard(hazard_checker_1_ex_hazard));
  Memory_Hazard_Checker memory_hazard_checker_1 (
    .MEM_WB_RegWrite(MEM_WB_RegWrite), .MEM_WB_RD(MEM_WB_RegisterRd), .ID_EX_Rs(ID_EX_RegisterRs),
    .EX_Hazard(hazard_checker_1_ex_hazard), .MEM_Hazard(Forward[0]));
  not not_1 (not_1_out, Forward[0]);
  and and_1 (Forward[1], hazard_checker_1_ex_hazard, not_1_out);
endmodule

module Forwarding_Unit (
  input  EX_MEM_RegWrite,
  input  [3:0] EX_MEM_RegisterRd,
  input  MEM_WB_RegWrite,
  input  [3:0] MEM_WB_RegisterRd,
  input  [3:0] ID_EX_RegisterRs,
  input  [3:0] ID_EX_RegisterRt,
  output [1:0] Forward_A,
  output [1:0] Forward_B
);

  Forward_Bit_Generator Forward_A_Generator (
    .EX_MEM_RegWrite(EX_MEM_RegWrite), .EX_MEM_RegisterRd(EX_MEM_RegisterRd),
    .ID_EX_RegisterRs(ID_EX_RegisterRs), .MEM_WB_RegWrite(MEM_WB_RegWrite),
    .MEM_WB_RegisterRd(MEM_WB_RegisterRd), .Forward(Forward_A));
  Forward_Bit_Generator Forward_B_Generator (
    .EX_MEM_RegWrite(EX_MEM_RegWrite), .EX_MEM_RegisterRd(EX_MEM_RegisterRd),
    .ID_EX_RegisterRs(ID_EX_RegisterRt), .MEM_WB_RegWrite(MEM_WB_RegWrite),
    .MEM_WB_RegisterRd(MEM_WB_RegisterRd), .Forward(Forward_B));
endmodule
