// Logisim project MIPS.circ as structural Verilog: 6 circuits, main circuit main
module main (
  input  CLEAR,
  input  in_2
);

  wire clock_1_out;
  wire [1:0] forwarding_unit_1_forward_a, forwarding_unit_1_forward_b;
  wire [3:0] instructions_1__4_7, instructions_1__8_11, instructions_1__12_15, instructions_1__16_19,
       pipeline_register_1_out_11, pipeline_register_1_out_12, pipeline_register_1_out_13,
       pipeline_register_2_out_11, pipeline_register_2_out_12, pipeline_register_2_out_13,
       pipeline_register_3_out_11, pipeline_register_3_out_12, pipeline_register_3_out_13,
       pipeline_register_4_out_13;
  wire [7:0] adder_1_out, alu_1_f, multiplexer_1_out, multiplexer_2_out, multiplexer_3_out, PC_q,
       pipeline_register_2_out_9, pipeline_register_2_out_10, pipeline_register_3_out_9,
       pipeline_register_3_out_10, pipeline_register_4_out_9, pipeline_register_4_out_10, ram_1_data,
       register_file_1_read_data_1, register_file_1_read_data_2;
  wire [11:0] control_1_out_2, pipeline_register_1_out_8, pipeline_register_2_out_8,
       pipeline_register_3_out_8, pipeline_register_4_out_8;

  Clock clock_1 (.out(clock_1_out));
  Register #(.trigger("falling")) PC (.D(adder_1_out), .Q(PC_q), .clk(clock_1_out), .clr(CLEAR));  // open: en
  Adder adder_1 (.a(PC_q), .b(8'h1), .out(adder_1_out));  // open: cin, cout
  Instructions instructions_1 (
    .PC(PC_q), ._16_19(instructions_1__16_19), ._12_15(instructions_1__12_15), ._8_11(instructions_1__8_11),
    ._4_7(instructions_1__4_7));  // open: _0_3
  Pipeline_Register pipeline_register_1 (
    .in_2({instructions_1__16_19, {8{1'b0}}}), .in_5(instructions_1__12_15), .in_6(instructions_1__8_11),
    .in_7(instructions_1__4_7), .out_8(pipeline_register_1_out_8), .out_11(pipeline_register_1_out_11),
    .out_12(pipeline_register_1_out_12), .out_13(pipeline_register_1_out_13), .in_1(clock_1_out));  // open: in_4, out_9, out_10, in_3
  Control control_1 (.OP_Code(pipeline_register_1_out_8[11:8]), .out_2(control_1_out_2));
  Register_File register_file_1 (
    .Dst_Reg_1(pipeline_register_4_out_13), .Write_Data(multiplexer_3_out),
    .Src_Reg_1(pipeline_register_1_out_11), .Src_Reg_2(pipeline_register_1_out_12),
    .RegWrite(pipeline_register_4_out_8[8]), .Read_Data_1(register_file_1_read_data_1),
    .Read_Data_2(register_file_1_read_data_2), .clk_prime(clock_1_out));
  Pipeline_Register pipeline_register_2 (
    .in_2(control_1_out_2), .in_4(register_file_1_read_data_2), .in_5(pipeline_register_1_out_11),
    .in_6(pipeline_register_1_out_12), .in_7(pipeline_register_1_out_13), .out_8(pipeline_register_2_out_8),
    .out_9(pipeline_register_2_out_9), .out_10(pipeline_register_2_out_10),
    .out_11(pipeline_register_2_out_11), .out_12(pipeline_register_2_out_12),
    .out_13(pipeline_register_2_out_13), .in_1(clock_1_out));  // open: in_3
  Multiplexer #(.select(2), .width(8), .enable("false")) multiplexer_1 (
    .in0(pipeline_register_2_out_9), .in1(multiplexer_3_out), .in2(pipeline_register_3_out_9),
    .out(multiplexer_1_out), .sel(forwarding_unit_1_forward_a));  // open: in3
  Multiplexer #(.select(2), .width(8), .enable("false")) multiplexer_2 (
    .in0(pipeline_register_2_out_10), .in1(multiplexer_3_out), .in2(pipeline_register_3_out_9),
    .out(multiplexer_2_out), .sel(forwarding_unit_1_forward_b));  // open: in3
  ALU alu_1 (
    .A(multiplexer_1_out), .B(multiplexer_2_out), .ALUop(pipeline_register_2_out_8[2:0]), .F(alu_1_f));  // open: ZF
  Forwarding_Unit forwarding_unit_1 (
    .EX_MEM_RegWrite(pipeline_register_3_out_8[8]), .EX_MEM_RegisterRd(pipeline_register_3_out_13),
    .MEM_WB_RegWrite(pipeline_register_4_out_8[8]), .MEM_WB_RegisterRd(pipeline_register_4_out_13),
    .ID_EX_RegisterRs(pipeline_register_2_out_11), .ID_EX_RegisterRt(pipeline_register_2_out_12),
    .Forward_A(forwarding_unit_1_forward_a), .Forward_B(forwarding_unit_1_forward_b));
  Pipeline_Register pipeline_register_3 (
    .in_2(pipeline_register_2_out_8), .in_4(pipeline_register_2_out_10), .in_5(pipeline_register_2_out_11),
    .in_6(pipeline_register_2_out_12), .in_7(pipeline_register_2_out_13), .out_8(pipeline_register_3_out_8),
    .out_9(pipeline_register_3_out_9), .out_10(pipeline_register_3_out_10),
    .out_11(pipeline_register_3_out_11), .out_12(pipeline_register_3_out_12),
    .out_13(pipeline_register_3_out_13), .in_1(clock_1_out));  // open: in_3
  RAM #(.bus("separate")) ram_1 (
    .addr(pipeline_register_3_out_9), .din(pipeline_register_3_out_10), .data(ram_1_data),
    .str(pipeline_register_3_out_8[6]), .clk(clock_1_out), .ld(pipeline_register_3_out_8[7]));  // open: sel, clr
  Pipeline_Register pipeline_register_4 (
    .in_2(pipeline_register_3_out_8), .in_4(ram_1_data), .in_5(pipeline_register_3_out_11),
    .in_6(pipeline_register_3_out_12), .in_7(pipeline_register_3_out_13), .out_8(pipeline_register_4_out_8),
    .out_9(pipeline_register_4_out_9), .out_10(pipeline_register_4_out_10),
    .out_13(pipeline_register_4_out_13), .in_1(clock_1_out));  // open: out_11, out_12, in_3
  Multiplexer #(.width(8), .enable("false")) multiplexer_3 (
    .in0(pipeline_register_4_out_9), .in1(pipeline_register_4_out_10), .out(multiplexer_3_out),
    .sel(pipeline_register_4_out_8[9]));

  // Notes on the sheet:
  //   Instruction Memory
  //   Forwarding Unit
  //   Data Memory
endmodule

module Register_File (
  input  RegWrite,
  input  clk_prime,
  input  [3:0] Dst_Reg_1,
  input  [7:0] Write_Data,
  input  [3:0] Src_Reg_1,
  input  [3:0] Src_Reg_2,
  output [7:0] Read_Data_1,
  output [7:0] Read_Data_2
);

  wire and_1_out, demultiplexer_1_out1, demultiplexer_1_out2, demultiplexer_1_out3, demultiplexer_1_out4,
       demultiplexer_1_out5, demultiplexer_1_out6, demultiplexer_1_out7;
  wire [7:0] _0___zero_q, _1___t0_q, _2___t1_q, _3___t2_q, _4___t3_q, _5___t4_q, _6___sp_q, _7___t5_q;

  Register _0___zero (.Q(_0___zero_q));  // open: D, en, clk, clr
  Register _1___t0 (.D(Write_Data), .Q(_1___t0_q), .clk(demultiplexer_1_out1));  // open: en, clr
  Register _2___t1 (.D(Write_Data), .Q(_2___t1_q), .clk(demultiplexer_1_out2));  // open: en, clr
  Multiplexer #(.select(3), .width(8), .enable("false")) multiplexer_1 (
    .in0(_0___zero_q), .in1(_1___t0_q), .in2(_2___t1_q), .in3(_3___t2_q), .in4(_4___t3_q), .in5(_5___t4_q),
    .in6(_6___sp_q), .in7(_7___t5_q), .out(Read_Data_1), .sel(Src_Reg_1[2:0]));
  Demultiplexer #(.select(3), .enable("false")) demultiplexer_1 (
    .out1(demultiplexer_1_out1), .out2(demultiplexer_1_out2), .out3(demultiplexer_1_out3),
    .out4(demultiplexer_1_out4), .out5(demultiplexer_1_out5), .out6(demultiplexer_1_out6),
    .out7(demultiplexer_1_out7), .in(and_1_out), .sel(Dst_Reg_1[2:0]));  // open: out0
  Register _3___t2 (.D(Write_Data), .Q(_3___t2_q), .clk(demultiplexer_1_out3));  // open: en, clr
  and and_1 (and_1_out, RegWrite, clk_prime);
  Register _4___t3 (.D(Write_Data), .Q(_4___t3_q), .clk(demultiplexer_1_out4));  // open: en, clr
  Multiplexer #(.select(3), .width(8), .enable("false")) multiplexer_2 (
    .in0(_0___zero_q), .in1(_1___t0_q), .in2(_2___t1_q), .in3(_3___t2_q), .in4(_4___t3_q), .in5(_5___t4_q),
    .in6(_6___sp_q), .in7(_7___t5_q), .out(Read_Data_2), .sel(Src_Reg_2[2:0]));
  Register _5___t4 (.D(Write_Data), .Q(_5___t4_q), .clk(demultiplexer_1_out5));  // open: en, clr
  Register _6___sp (.D(Write_Data), .Q(_6___sp_q), .clk(demultiplexer_1_out6));  // open: en, clr
  Register _7___t5 (.D(Write_Data), .Q(_7___t5_q), .clk(demultiplexer_1_out7));  // open: en, clr
endmodule

module Instructions (
  input  [7:0] PC,
  output [3:0] _16_19,
  output [3:0] _12_15,
  output [3:0] _8_11,
  output [3:0] _4_7,
  output [3:0] _0_3
);

  ROM #(.dataWidth(20)) rom_1 (.addr(PC), .data({_16_19, _12_15, _8_11, _4_7, _0_3}));  // open: sel

  // Notes on the sheet:
  //   contents of rom_1 (hex, n*v repeats v):
  //   13420 b2350 22450 15450
endmodule

module Control (
  input  [3:0] OP_Code,
  output [11:0] out_2
);

  ROM #(.addrWidth(4), .dataWidth(12)) rom_1 (.addr(OP_Code), .data(out_2));  // open: sel

  // Notes on the sheet:
  //   contents of rom_1 (hex, n*v repeats v):
  //   8 900 902 11 440 21 501 780 503 904 502 901 506 903 505 500
endmodule

module ALU (
  input  [7:0] A,
  input  [7:0] B,
  input  [2:0] ALUop,
  output ZF,
  output [7:0] F
);

  wire [7:0] adder_1_out, and_1_out, nor_1_out, or_1_out, subtractor_1_out;
  wire [15:0] shifter_1_out, shifter_2_out;

  Adder adder_1 (.a(A), .b(B), .out(adder_1_out), .cin(1'b0));  // open: cout
  Subtractor subtractor_1 (.a(A), .b(B), .out(subtractor_1_out), .bin(1'b0));  // open: bout
  assign or_1_out = A | B;  // OR_Gate or_1, 8 bits wide
  assign and_1_out = A & B;  // AND_Gate and_1, 8 bits wide
  assign nor_1_out = ~(A | B);  // NOR_Gate nor_1, 8 bits wide
  Shifter #(.width(16)) shifter_1 (.in({{8{1'b0}}, A}), .\dist (B[3:0]), .out(shifter_1_out));
  Shifter #(.width(16), .shift("lr")) shifter_2 (.in({{8{1'b0}}, A}), .\dist (B[3:0]), .out(shifter_2_out));
  Multiplexer #(.select(3), .width(8), .enable("false")) multiplexer_1 (
    .in0(adder_1_out), .in1(subtractor_1_out), .in2(or_1_out), .in3(and_1_out), .in4(nor_1_out),
    .in5(shifter_1_out[7:0]), .in6(shifter_2_out[7:0]), .in7({8{1'b0}}), .out(F), .sel(ALUop));
  nor nor_2 (ZF, F[0], F[1], F[2], F[3], F[4], F[5], F[6], F[7]);
endmodule

module Pipeline_Register (
  input  in_1,
  input  [11:0] in_2,
  input  [7:0] in_3,
  input  [7:0] in_4,
  input  [3:0] in_5,
  input  [3:0] in_6,
  input  [3:0] in_7,
  output [11:0] out_8,
  output [7:0] out_9,
  output [7:0] out_10,
  output [3:0] out_11,
  output [3:0] out_12,
  output [3:0] out_13
);

  wire not_1_out;

  not not_1 (not_1_out, in_1);
  Register #(.width(12)) Control (.D(in_2), .Q(out_8), .clk(not_1_out));  // open: en, clr
  Register Data1 (.D(in_3), .Q(out_9), .clk(not_1_out));  // open: en, clr
  Register Data2 (.D(in_4), .Q(out_10), .clk(not_1_out));  // open: en, clr
  Register #(.width(4)) RS (.D(in_5), .Q(out_11), .clk(not_1_out));  // open: en, clr
  Register #(.width(4)) RT (.D(in_6), .Q(out_12), .clk(not_1_out));  // open: en, clr
  Register #(.width(4)) RD (.D(in_7), .Q(out_13), .clk(not_1_out));  // open: en, clr
endmodule
